// Digital circuit InstDecoder.dig as structural Verilog
module InstDecoder (
  input  [31:0] IW,
  output [1:0] ALUSrcB,
  output ALUSrcA,
  output [2:0] ALUOp,
  output RFW,
  output WDsel,
  output PCsel
);

  wire add_i_1_eq, add_r_1_eq, jal_1_eq, jalr_1_p3, mul_1_eq, sll_1_eq, slli_1_eq, srl_1_eq, srli_1_eq;
  wire [3:0] priorityencoder_1_num;

  add_i add_i_1 (.opcode(IW[6:0]), .funct3(IW[14:12]), .eq(add_i_1_eq));
  add_r add_r_1 (.opcode(IW[6:0]), .funct3(IW[14:12]), .funct7(IW[31:25]), .eq(add_r_1_eq));
  jal jal_1 (.opcode(IW[6:0]), .eq(jal_1_eq));
  // jalr jalr_1: pin names not known; wires that end beside it: IW[6:0], IW[14:12], jalr_1_p3
  mul mul_1 (.opcode(IW[6:0]), .funct3(IW[14:12]), .funct7(IW[31:25]), .eq(mul_1_eq));
  sll sll_1 (.opcode(IW[6:0]), .funct3(IW[14:12]), .funct7(IW[31:25]), .eq(sll_1_eq));
  slli slli_1 (.opcode(IW[6:0]), .funct3(IW[14:12]), .funct7(IW[31:25]), .eq(slli_1_eq));
  srl srl_1 (.opcode(IW[6:0]), .funct3(IW[14:12]), .funct7(IW[31:25]), .eq(srl_1_eq));
  srli srli_1 (.opcode(IW[6:0]), .funct3(IW[14:12]), .funct7(IW[31:25]), .eq(srli_1_eq));
  PriorityEncoder #(.Selector_Bits(4)) priorityencoder_1 (
    .in0(add_i_1_eq), .in1(add_r_1_eq), .in2(jal_1_eq), .in3(jalr_1_p3), .in4(mul_1_eq), .in5(sll_1_eq),
    .in6(slli_1_eq), .in7(srl_1_eq), .in8(srli_1_eq), .in9(1'b0), .in10(1'b0), .in11(1'b0), .in12(1'b0),
    .in13(1'b0), .in14(1'b0), .in15(1'b0), .num(priorityencoder_1_num));  // open: any
  ROM #(.AddrBits(4), .Bits(9)) rom_1 (
    .A(priorityencoder_1_num), .sel(1'b1), .D({RFW, ALUOp, ALUSrcA, ALUSrcB, PCsel, WDsel}));

  // Other names for the same wires on the sheet: opcode[6:0] = IW[6:0]; funct3[2:0] = IW[14:12];
  //   funct7[6:0] = IW[31:25]

  // Notes on the sheet:
  //   contents of rom_1 (hex, n*v repeats v):
  //   104,100,11b,107,140,160,164,180,184
endmodule
